# Fritzing sketch Residência - Kit Sensores V1 (saved by Fritzing 1.0.7)
breadboards: 1

parts:
  Part1 = InvenSense MPU6050
  M1 = DOIT Esp32 DevKit v1 (30 pins long, 11 pins width) [part_number=ESP32S-PIN30]
  Part2 = Adafruit VL53L1X [part_number="Adafruit #3967"]
  HC-SR04_Sensor_1 = HC-SR04 Ultrasonic Distance Sensor
  R1 = Resistor [tolerance=±5% power=0.25W resistance=1 package=THT]
  R2 = Resistor [tolerance=±5% power=0.25W resistance=2.2 package=THT]
  Part3 = Adafruit INA219 Current Sensor FeatherWing [part_number=3650]  # not connected

nets:
  VCC: Part1.VCC, M1.3V3, Part2.VCC
  GND: Part1.GND, M1.GND, Part2.GND, HC-SR04_Sensor_1.GND, R2.Pin_0
  N1: Part1.SCL, M1.D22, Part2.SCL
  N2: Part1.SDA, M1.D21, Part2.SDA
  N3: M1.D5, HC-SR04_Sensor_1.TRIG
  N4: M1.D18, R1.Pin_0, R2.Pin_1
  VIN: M1.VIN, HC-SR04_Sensor_1.VCC
  N5: HC-SR04_Sensor_1.ECHO, R1.Pin_1

notes:
  vermelho = 3,3V, laranja = 5V, preto = GND, amarelo = SDA, verde = SCL, branco = TRIG/ECHO/XSHUT.

custom parts:
  DOIT Esp32 DevKit v1 (30 pins long, 11 pins width): The DOIT Esp32 DevKit v1 is one of the development board created by DOIT to evaluate the ESP-WROOM-32 module. It is based on the ESP32 microcontroller that boasts Wifi, Bluetooth, Ethernet and Low Power support all in a single chip. (vanepp) made breadboard work, adjusted pin numbering and labels and reduced size of schematic and cleaned up pcb. This chip is 30pins long (2 x15) and 11 pins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
  Adafruit VL53L1X: The Adafruit VL53L1X Time of Flight Distance Sensor (also known as VL53L1CX) is a Time of Flight distance sensor that has a massive 4 meter range and LIDAR-like precision. The sensor contains a very tiny invisible laser source and a matching sensor. The VL53L1X can detect the "time of flight", or how long the light has taken to bounce back to the sensor. Since it uses a very narrow light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

// code stored in the sketch: Resid├¬ncia - Kit Sensores V1.ino
#include <Wire.h>

void setup() {
  Wire.begin(21, 22); // SDA, SCL
  Serial.begin(115200);
  delay(1000);
  Serial.println("Escaneando I2C...");
}

void loop() {
  for (byte addr = 1; addr < 127; addr++) {
    Wire.beginTransmission(addr);
    if (Wire.endTransmission() == 0) {
      Serial.print("Dispositivo encontrado em 0x");
      Serial.println(addr, HEX);
    }
  }
  delay(3000);
}
